// Digital circuit control_unit.dig as structural Verilog
module control_unit (
  input  nirq,
  input  clk,
  input  [7:0] opcode,
  input  [4:0] flags,
  input  nrst,
  input  nreq,
  output [3:0] dbus_assert,
  output [3:0] dbus_load,
  output [4:0] alu_op,
  output [4:0] xfer_assert,
  output [2:0] xfer_load,
  output [2:0] addr_assert,
  output [2:0] count,
  output dec_sp,
  output nbrk,
  output nclk
);

  wire clk_inverter_p2, clk_inverter_p3, clk_inverter_p4, clk_inverter_p5, clk_inverter_p6, rst_useq,
       sequencer_p1, sequencer_p2, sequencer_p4, sequencer_p5, sequencer_p6;
  wire [1:0] m_tog;
  wire [2:0] t_state;
  wire [7:0] ucode_2_d, ucode_3_d, ucode_4_d, ucode_d;
  wire [7:1] Latch_IRQ_q;
  wire [16:16] ucode_addr;

  // _7404 clk_inverter: pin names not known; wires that end beside it: clk, clk_inverter_p2, clk_inverter_p3, clk_inverter_p4, clk_inverter_p5, clk_inverter_p6, 1'b1, 1'b0, nclk
  // NotConnected on clk_inverter_p2
  // NotConnected on clk_inverter_p3
  // NotConnected on clk_inverter_p4
  // NotConnected on clk_inverter_p5
  // NotConnected on clk_inverter_p6
  _74ls574 Latch_IRQ (
    .nOC(1'b0), .CLK(clk), .D({7'b0000001, nirq}), .VCC(1'b1), .GND(1'b0), .Q({Latch_IRQ_q, ucode_addr[16]}));
  // _74193 sequencer: pin names not known; wires that end beside it: sequencer_p1, sequencer_p2, clk, sequencer_p4, sequencer_p5, sequencer_p6, rst_useq, 1'b1, 1'b1, 1'b0, t_state[0], t_state[1], t_state[2]
  // NotConnected on sequencer_p1
  // NotConnected on sequencer_p2
  // NotConnected on sequencer_p4
  // NotConnected on sequencer_p5
  // NotConnected on sequencer_p6
  EEPROM #(.AddrBits(19), .Bits(8)) ucode (
    .A({2'b11, ucode_addr[16], opcode, flags, t_state}), .CS(1'b1), .WE(1'b0), .OE(1'b1), .D(ucode_d));
  EEPROM #(.AddrBits(19), .Bits(8)) ucode_2 (
    .A({2'b11, ucode_addr[16], opcode, flags, t_state}), .CS(1'b1), .WE(1'b0), .OE(1'b1), .D(ucode_2_d));
  EEPROM #(.AddrBits(19), .Bits(8)) ucode_3 (
    .A({2'b11, ucode_addr[16], opcode, flags, t_state}), .CS(1'b1), .WE(1'b0), .OE(1'b1), .D(ucode_3_d));
  EEPROM #(.AddrBits(19), .Bits(8)) ucode_4 (
    .A({2'b11, ucode_addr[16], opcode, flags, t_state}), .CS(1'b1), .WE(1'b0), .OE(1'b1), .D(ucode_4_d));
  _74ls574 _74ls574_1 (.nOC(nrst), .CLK(nclk), .D(ucode_d), .VCC(1'b1), .GND(1'b0), .Q({dbus_load, dbus_assert}));
  _74ls574 _74ls574_2 (.nOC(nrst), .CLK(nclk), .D(ucode_2_d), .VCC(1'b1), .GND(1'b0), .Q({xfer_assert[2:0], alu_op}));
  _74ls574 _74ls574_3 (
    .nOC(nrst), .CLK(nclk), .D(ucode_3_d), .VCC(1'b1), .GND(1'b0),
    .Q({addr_assert, xfer_load, xfer_assert[4:3]}));
  _74ls574 _74ls574_4 (
    .nOC(nrst), .CLK(nclk), .D(ucode_4_d), .VCC(1'b1), .GND(1'b0), .Q({nbrk, m_tog, rst_useq, dec_sp, count}));

  // Other names for the same wires on the sheet: xa_3 = xfer_assert[3]; xa_4 = xfer_assert[4]; xa_0 = xfer_assert[0];
  //   xa_1 = xfer_assert[1]; xa_2 = xfer_assert[2]; ucode_addr[15:0] = {opcode, flags, t_state}
endmodule
